# Fritzing sketch Fritzing-Bootloading (saved by Fritzing 0.9.3b)
circuit board: 9.77008cm x 2.12527cm
breadboards: 2

parts:
  U1 = atmega328 [package=dip]
  U2 = atmega328 [package=dip]
  R1 = Resistor [tolerance=±5% resistance=10k package="0805 [SMD]"]
  Part1 = FTDI Basic Programmer
  C3 = Tantalum Capacitor [capacitance=0.1µF package="200 mil [THT, tantalum]"]
  C4 = Tantalum Capacitor [capacitance=0.1µF package="200 mil [THT, tantalum]"]

nets:
  N1: U1.RESET, R1.Pin_1, C4.-
  N2: U1.D0_(RX), Part1.TXO
  N3: U1.D1_(TX), Part1.RXI
  VCC: U1.VCC, U2.VCC, R1.Pin_0, Part1.POWER, C3.-
  N4: U1.GND#7, U2.GND#7, Part1.GND, C3.+
  N5: U1.D10_(PWM), U2.RESET
  N6: U1.D11_(PWM), U2.D11_(PWM)
  N7: U1.D12, U2.D12
  N8: U1.D13, U2.D13
  N9: Part1.DTR, C4.+

notes:
  (MASTER) - Arduino Installer
  (SLAVE) - RAW Arduino Chip
