# Fritzing sketch Fritzing- Programming (saved by Fritzing 0.9.3b)
circuit board: 4.24226cm x 1.78656cm
breadboards: 1

parts:
  U1 = atmega328 [package=dip]
  R1 = Resistor [tolerance=±5% resistance=10k package="0603 [SMD]"]
  Part1 = FTDI Basic Programmer
  C3 = Tantalum Capacitor [capacitance=0.1µF package="100 mil [THT, tantalum]"]
  C4 = Tantalum Capacitor [capacitance=0.1µF package="100 mil [THT, tantalum]"]

nets:
  N1: U1.RESET, R1.Pin_1, C3.-
  N2: U1.D0_(RX), Part1.TXO
  N3: U1.D1_(TX), Part1.RXI
  N4: U1.VCC, R1.Pin_0, Part1.POWER, C4.-
  N5: U1.GND#7, Part1.GND, C4.+
  N6: Part1.DTR, C3.+

notes:
  Arduino Chip with Bootloader
  - This does not have a 16MHz Crystal
  - This requires at least 8 male-male jumpers
  - This uses the SparkFun FTDI Breakout/Cable
  - Plug&Play when using macOS High Sierra or higher or Windows 10+
